# Fritzing sketch ledcube (saved by Fritzing 0.7.11b)
breadboards: 1

parts:
  LED1 = LED - 5mm [color="Red (633nm)" package="5 mm [THT]"]
  LED2 = LED - 5mm [color="Red (633nm)" package="5 mm [THT]"]
  LED3 = LED - 5mm [color="Red (633nm)" package="5 mm [THT]"]
  LED4 = LED - 5mm [color="Red (633nm)" package="5 mm [THT]"]
  LED5 = LED - 5mm [color="Red (633nm)" package="5 mm [THT]"]
  LED6 = LED - 5mm [color="Red (633nm)" package="5 mm [THT]"]
  LED7 = LED - 5mm [color="Red (633nm)" package="5 mm [THT]"]
  LED8 = LED - 5mm [color="Red (633nm)" package="5 mm [THT]"]
  U1 = 74HC595 [package="DIP16 [THT]"]
  Q1 = NPN-Transistor [package="TO92 [THT]"]
  R1 = Resistor [tolerance=±5% resistance=220 package=THT]
  R2 = Resistor [tolerance=±5% resistance=220 package=THT]
  R3 = Resistor [tolerance=±5% resistance=220 package=THT]
  R4 = Resistor [tolerance=±5% resistance=220 package=THT]
  R5 = Resistor [tolerance=±5% resistance=220 package=THT]
  R6 = Resistor [tolerance=±5% resistance=220 package=THT]
  R7 = Resistor [tolerance=±5% resistance=220 package=THT]
  R8 = Resistor [tolerance=±5% resistance=220 package=THT]
  Arduino1 = Arduino
  U2 = 74HC138 [package="DIP16 [THT]"]

nets:
  N1: LED1.cathode, LED2.cathode, LED3.cathode, LED4.cathode, LED5.cathode, LED6.cathode, LED7.cathode, LED8.cathode, Q1.C
  N2: LED1.anode, R4.Pin_0
  N3: LED2.anode, R5.Pin_0
  N4: LED3.anode, R6.Pin_0
  N5: LED4.anode, R7.Pin_0
  N6: LED5.anode, R2.Pin_0
  N7: LED6.anode, R3.Pin_0
  N8: LED7.anode, R1.Pin_0
  N9: LED8.anode, R8.Pin_0
  N10: U1.Q1, R8.Pin_1
  N11: U1.Q2, R7.Pin_1
  N12: U1.Q3, R6.Pin_1
  N13: U1.Q4, R5.Pin_1
  N14: U1.Q5, R4.Pin_1
  N15: U1.Q6, R3.Pin_1
  N16: U1.Q7, R2.Pin_1
  GND: U1.GND, Q1.E
  N17: U1.SH_CP, U1.ST_CP, Arduino1.D8
  N18: U1.OE, Arduino1.D9
  N19: U1.DS, Arduino1.D10
  N20: U1.Q0, R1.Pin_1
  5V: U1.VCC
  N21: Q1.B, U2.Q0
  N22: Arduino1.D13, U2.Q1
  N23: Arduino1.D12, U2.Q2
  N24: Arduino1.D11, U2.Q3

custom parts:
  74HC138: 3 to 8 line decoder
